// Logisim project ddca expo.circ as structural Verilog: 1 circuit, main circuit main
module main (
  input  in_1,
  input  in_2,
  input  in_3,
  input  in_4,
  output out_5,
  output out_6,
  output out_7,
  output out_8
);

  wire clock_1_out, d_ff_1_q, d_ff_2_q, d_ff_3_q, d_ff_4_q, multiplexer_1_out, multiplexer_2_out,
       multiplexer_3_out, multiplexer_4_out;

  Clock clock_1 (.out(clock_1_out));
  Multiplexer multiplexer_1 (.in0(in_1), .in1(in_3), .out(multiplexer_1_out));  // open: sel, en
  D_Flip_Flop d_ff_1 (.D(multiplexer_1_out), .Q(d_ff_1_q), .en(clock_1_out));  // open: clk, Qn, preset, reset
  Multiplexer multiplexer_2 (.in0(in_1), .in1(in_3), .out(multiplexer_2_out));  // open: sel, en
  D_Flip_Flop d_ff_2 (.D(multiplexer_2_out), .Q(d_ff_2_q), .en(clock_1_out));  // open: clk, Qn, preset, reset
  Multiplexer multiplexer_3 (.in0(in_1), .in1(in_3), .out(multiplexer_3_out));  // open: sel, en
  D_Flip_Flop d_ff_3 (.D(multiplexer_3_out), .Q(d_ff_3_q), .en(clock_1_out));  // open: clk, Qn, preset, reset
  Multiplexer multiplexer_4 (.in0(in_1), .in1(in_3), .out(multiplexer_4_out));  // open: sel, en
  D_Flip_Flop d_ff_4 (.D(multiplexer_4_out), .Q(d_ff_4_q), .en(clock_1_out));  // open: clk, Qn, preset, reset
endmodule
